# Fritzing sketch Motorcycle_Security_Scheme (saved by Fritzing 0.9.3b)

parts:
  WeMos_D1_Mini1 = WeMos D1 Mini
  Part1 = RFID-RC522-v2
  KF-1 = KF-301 Relay [package=THT]

nets:
  3V3: WeMos_D1_Mini1.3V3, Part1.3.3V
  N1: WeMos_D1_Mini1.D0, KF-1.signal
  N2: WeMos_D1_Mini1.D3, Part1.RST
  N3: WeMos_D1_Mini1.D5, Part1.SCK
  N4: WeMos_D1_Mini1.D6, Part1.MISO
  N5: WeMos_D1_Mini1.D7, Part1.MOSI
  N6: WeMos_D1_Mini1.D8, Part1.SDA
  N7: WeMos_D1_Mini1.G, Part1.GND

custom parts:
  RFID-RC522-v2: A simple China made RFID-RC522 Reader; do check the pin labels, as this is a MFRC522 based clone.
  KF-301 Relay: KF-301
